# Fritzing sketch Stepper Motor Connection Schematic (saved by Fritzing 0.9.4)
breadboards: 1

parts:
  part = Raspberry Pi B+
  Stepper_B = Stepper Motor - Bipolar
  Stepper_Driver_B = Pololu A4988 [package=SO16]
  Stepper_Power = DC Power [voltage=16.5 frequency=60]
  Stepper_Driver_A = Pololu A4988 [package=SO16]
  Stepper_A = Stepper Motor - Bipolar

nets:
  VDD: part.3v3, Stepper_Driver_B.VDD, Stepper_Driver_A.VDD
  N1: part.GPIO6, Stepper_Driver_A.DIR
  N2: part.GPIO13, Stepper_Driver_A.STEP
  N3: part.GPIO19, Stepper_Driver_B.DIR
  N4: part.GPIO26, Stepper_Driver_B.STEP
  N5: part.GND, Stepper_Driver_B.GND#8, Stepper_Driver_A.GND#8
  N6: Stepper_B.A, Stepper_Driver_B.2B
  N7: Stepper_B.C, Stepper_Driver_B.2A
  N8: Stepper_B.B, Stepper_Driver_B.1A
  N9: Stepper_B.D, Stepper_Driver_B.1B
  N10: Stepper_Driver_B.RESET, Stepper_Driver_B.SLEEP
  N11: Stepper_Driver_B.GND#14, Stepper_Power.V-, Stepper_Driver_A.GND#14
  N12: Stepper_Driver_B.VMOT, Stepper_Power.V+, Stepper_Driver_A.VMOT
  N13: Stepper_Driver_A.RESET, Stepper_Driver_A.SLEEP
  N14: Stepper_Driver_A.1B, Stepper_A.D
  N15: Stepper_Driver_A.1A, Stepper_A.B
  N16: Stepper_Driver_A.2A, Stepper_A.C
  N17: Stepper_Driver_A.2B, Stepper_A.A
